// Logisim project Calculadora Digital.circ as structural Verilog
module somador (
  input  A0,
  input  B0,
  input  A1,
  input  B1,
  input  A2,
  input  B2,
  input  A3,
  input  B3
);
endmodule
